// Logisim project CRC.circ as structural Verilog: 2 circuits, main circuit CRC
module CRC (
  input  [7:0] in_1,
  input  [3:0] in_2,
  output [10:0] out_3
);

  wire [2:0] mod_1_out_3, mod_2_out_3, mod_3_out_3, mod_4_out_3, mod_5_out_3, mod_6_out_3, mod_7_out_3;

  // Probe on in_1[7:4]
  // Probe on mod_1_out_3
  mod mod_1 (.in_1(in_1[7:4]), .in_2(in_2), .out_3(mod_1_out_3));
  // Probe on mod_2_out_3
  mod mod_2 (.in_1({mod_1_out_3, in_1[3]}), .in_2(in_2), .out_3(mod_2_out_3));
  mod mod_3 (.in_1({mod_2_out_3, in_1[2]}), .in_2(in_2), .out_3(mod_3_out_3));
  // Probe on mod_3_out_3
  // Probe on mod_4_out_3
  mod mod_4 (.in_1({mod_3_out_3, in_1[1]}), .in_2(in_2), .out_3(mod_4_out_3));
  // Probe on mod_5_out_3
  mod mod_5 (.in_1({mod_4_out_3, in_1[0]}), .in_2(in_2), .out_3(mod_5_out_3));
  // Probe on mod_6_out_3
  mod mod_6 (.in_1({mod_5_out_3, 1'b0}), .in_2(in_2), .out_3(mod_6_out_3));
  mod mod_7 (.in_1({mod_6_out_3, 1'b0}), .in_2(in_2), .out_3(mod_7_out_3));
  // Probe on mod_7_out_3
  mod mod_8 (.in_1({mod_7_out_3, 1'b0}), .in_2(in_2), .out_3(out_3[2:0]));
  // Probe on in_1

  assign out_3[10:3] = in_1;

  // Other names for the same wires on the sheet: In[3:0] = in_2
endmodule

module mod (
  input  [3:0] in_1,
  input  [3:0] in_2,
  output [2:0] out_3
);

  wire [3:0] multiplexer_1_out;
  wire [3:3] xor_1_out;

  Multiplexer #(.width(4)) multiplexer_1 (
    .in0(4'b0000), .in1(in_2), .out(multiplexer_1_out), .sel(in_1[3]));  // open: en
  assign {xor_1_out[3], out_3} = in_1 ^ multiplexer_1_out;  // XOR_Gate xor_1, 4 bits wide
endmodule
