// Logisim project Cha.circ as structural Verilog: 5 circuits, main circuit main
module main (
  input  [31:0] in_1,
  output [31:0] out_2
);

  wire clock_1_out, clock_2_out, clock_3_out, comparator_1_eq, comparator_2_eq, counter_1_q, not_1_out;
  wire [31:0] multiplexer_1_out, multiplexer_2_out, register_1_q, s0_1_out_2, shifter_1_out;

  Counter #(.width(1), .max('h1), .ongoal("stay")) counter_1 (
    .Q(counter_1_q), .clk(not_1_out));  // open: load, D, count, carry, clr
  not not_1 (not_1_out, clock_1_out);
  Clock clock_1 (.out(clock_1_out));
  Comparator #(.width(1), .mode("unsigned")) comparator_1 (
    .a(1'b0), .b(counter_1_q), .eq(comparator_1_eq));  // open: gt, lt
  Multiplexer #(.width(32)) multiplexer_1 (
    .in0(shifter_1_out), .in1(in_1), .out(multiplexer_1_out), .sel(comparator_1_eq));  // open: en
  Clock clock_2 (.out(clock_2_out));
  Register #(.width(32)) register_1 (.D(multiplexer_1_out), .Q(register_1_q), .clk(clock_2_out));  // open: en, clr
  S0 s0_1 (.in_1(multiplexer_1_out), .out_2(s0_1_out_2));
  // Probe on shifter_1_out
  Shifter #(.width(32), .shift("lr")) shifter_1 (.in(register_1_q), .\dist (5'b00001), .out(shifter_1_out));
  Comparator #(.width(32), .mode("unsigned")) comparator_2 (
    .a(shifter_1_out), .b({32{1'b0}}), .eq(comparator_2_eq));  // open: gt, lt
  Multiplexer #(.width(32)) multiplexer_2 (
    .in0({32{1'b0}}), .in1(s0_1_out_2), .out(multiplexer_2_out), .sel(comparator_2_eq));  // open: en
  Clock clock_3 (.out(clock_3_out));
  Register #(.width(32)) register_2 (.D(multiplexer_2_out), .Q(out_2), .clk(clock_3_out));  // open: en, clr
endmodule

module S0 (
  input  [31:0] in_1,
  output [31:0] out_2
);

  wire comparator_1_eq;
  wire [31:0] _1, _2, _3, _4, _5, _6, _7, _8, A, and_1_out, B, D, E, F, G, H;

  assign and_1_out = in_1 & 32'h1;  // AND_Gate and_1, 32 bits wide
  base base (.in_1(_5), .in_2(_6), .in_3(_7), .in_4(_8), .out_5(E), .out_6(F), .out_7(G), .out_8(H));
  Comparator #(.width(32), .mode("unsigned")) comparator_1 (
    .a(and_1_out), .b({32{1'b0}}), .eq(comparator_1_eq));  // open: gt, lt
  ans ans (
    .in_2(_1), .in_3(_2), .in_4(_3), .in_5(_4), .in_1(comparator_1_eq), .out_6(A), .out_7(B), .out_8(out_2),
    .out_9(D));
  JZJS JS (
    .a1(A), .a2(B), .a3(out_2), .a4(D), .b1(E), .b2(F), .b3(G), .b4(H), .out_9(_1), .out_10(_2), .out_11(_3),
    .out_12(_4));
  JZJS JS_2 (
    .a1(E), .a2(F), .a3(G), .a4(H), .b1(E), .b2(F), .b3(G), .b4(H), .out_9(_5), .out_10(_6), .out_11(_7),
    .out_12(_8));
  // Probe on A
  // Probe on out_2
  // Probe on E
  // Probe on G
  // Probe on B
  // Probe on D
  // Probe on F
  // Probe on H

  // Other names for the same wires on the sheet: C[31:0] = out_2
endmodule

module base (
  input  [31:0] in_1,
  input  [31:0] in_2,
  input  [31:0] in_3,
  input  [31:0] in_4,
  output [31:0] out_5,
  output [31:0] out_6,
  output [31:0] out_7,
  output [31:0] out_8
);

  wire clock_1_out, clock_2_out, comparator_1_eq, counter_1_q, not_1_out, not_2_out;
  wire [31:0] register_1_q, register_2_q, register_3_q, register_4_q;

  Register #(.width(32)) register_1 (.D(in_1), .Q(register_1_q), .clk(not_2_out));  // open: en, clr
  not not_1 (not_1_out, clock_1_out);
  Clock clock_1 (.out(clock_1_out));
  Register #(.width(32)) register_2 (.D(in_2), .Q(register_2_q), .clk(not_2_out));  // open: en, clr
  Register #(.width(32)) register_3 (.D(in_3), .Q(register_3_q), .clk(not_2_out));  // open: en, clr
  Register #(.width(32)) register_4 (.D(in_4), .Q(register_4_q), .clk(not_2_out));  // open: en, clr
  not not_2 (not_2_out, clock_2_out);
  Clock clock_2 (.out(clock_2_out));
  Counter #(.width(1), .max('h1), .ongoal("stay")) counter_1 (
    .Q(counter_1_q), .clk(not_1_out));  // open: load, D, count, carry, clr
  Multiplexer #(.width(32)) multiplexer_1 (
    .in0(register_1_q), .in1({32{1'b0}}), .out(out_5), .sel(comparator_1_eq));  // open: en
  Multiplexer #(.width(32)) multiplexer_2 (
    .in0(register_2_q), .in1(32'h1), .out(out_6), .sel(comparator_1_eq));  // open: en
  Multiplexer #(.width(32)) multiplexer_3 (
    .in0(register_3_q), .in1(32'h1), .out(out_7), .sel(comparator_1_eq));  // open: en
  Multiplexer #(.width(32)) multiplexer_4 (
    .in0(register_4_q), .in1(32'h1), .out(out_8), .sel(comparator_1_eq));  // open: en
  Comparator #(.width(1), .mode("unsigned")) comparator_1 (
    .a(1'b0), .b(counter_1_q), .eq(comparator_1_eq));  // open: gt, lt
endmodule

module ans (
  input  in_1,
  input  [31:0] in_2,
  input  [31:0] in_3,
  input  [31:0] in_4,
  input  [31:0] in_5,
  output [31:0] out_6,
  output [31:0] out_7,
  output [31:0] out_8,
  output [31:0] out_9
);

  wire clock_1_out, comparator_1_eq, not_1_out;
  wire [31:0] _1, multiplexer_1_out, multiplexer_2_out, multiplexer_3_out, multiplexer_4_out, register_1_q,
       register_2_q, register_3_q;

  not not_1 (not_1_out, in_1);
  Multiplexer #(.width(32)) multiplexer_1 (
    .in0(register_1_q), .in1(in_2), .out(multiplexer_1_out), .sel(not_1_out));  // open: en
  Multiplexer #(.width(32)) multiplexer_2 (
    .in0(register_2_q), .in1(in_3), .out(multiplexer_2_out), .sel(not_1_out));  // open: en
  Multiplexer #(.width(32)) multiplexer_3 (
    .in0(register_3_q), .in1(in_4), .out(multiplexer_3_out), .sel(not_1_out));  // open: en
  Multiplexer #(.width(32)) multiplexer_4 (.in0(_1), .in1(in_5), .out(multiplexer_4_out), .sel(not_1_out));  // open: en
  Clock clock_1 (.out(clock_1_out));
  Register #(.width(32)) register_1 (.D(multiplexer_1_out), .Q(register_1_q), .clk(clock_1_out));  // open: en, clr
  Register #(.width(32)) register_2 (.D(multiplexer_2_out), .Q(register_2_q), .clk(clock_1_out));  // open: en, clr
  Register #(.width(32)) register_3 (.D(multiplexer_3_out), .Q(register_3_q), .clk(clock_1_out));  // open: en, clr
  Register #(.width(32)) register_4 (.D(multiplexer_4_out), .Q(_1), .clk(clock_1_out));  // open: en, clr
  Comparator #(.width(32), .mode("unsigned")) comparator_1 (
    .a(_1), .b({32{1'b0}}), .eq(comparator_1_eq));  // open: gt, lt
  Multiplexer #(.width(32)) multiplexer_5 (
    .in0(register_1_q), .in1(32'h1), .out(out_6), .sel(comparator_1_eq));  // open: en
  Multiplexer #(.width(32)) multiplexer_6 (
    .in0(register_2_q), .in1({32{1'b0}}), .out(out_7), .sel(comparator_1_eq));  // open: en
  Multiplexer #(.width(32)) multiplexer_7 (
    .in0(register_3_q), .in1({32{1'b0}}), .out(out_8), .sel(comparator_1_eq));  // open: en
  Multiplexer #(.width(32)) multiplexer_8 (.in0(_1), .in1(32'h1), .out(out_9), .sel(comparator_1_eq));  // open: en
endmodule

module JZJS (
  input  [31:0] a1,
  input  [31:0] a2,
  input  [31:0] a3,
  input  [31:0] a4,
  input  [31:0] b1,
  input  [31:0] b2,
  input  [31:0] b3,
  input  [31:0] b4,
  output [31:0] out_9,
  output [31:0] out_10,
  output [31:0] out_11,
  output [31:0] out_12
);

  wire [31:0] multiplier_1_out, multiplier_2_out, multiplier_3_out, multiplier_4_out, multiplier_5_out,
       multiplier_6_out, multiplier_7_out, multiplier_8_out;

  Multiplier #(.width(32)) multiplier_1 (.a(a1), .b(b1), .out(multiplier_1_out));  // open: cin, cout
  Multiplier #(.width(32)) multiplier_2 (.a(a2), .b(b3), .out(multiplier_2_out));  // open: cin, cout
  Multiplier #(.width(32)) multiplier_3 (.a(a1), .b(b2), .out(multiplier_3_out));  // open: cin, cout
  Multiplier #(.width(32)) multiplier_4 (.a(a2), .b(b4), .out(multiplier_4_out));  // open: cin, cout
  Multiplier #(.width(32)) multiplier_5 (.a(a3), .b(b1), .out(multiplier_5_out));  // open: cin, cout
  Multiplier #(.width(32)) multiplier_6 (.a(a4), .b(b3), .out(multiplier_6_out));  // open: cin, cout
  Multiplier #(.width(32)) multiplier_7 (.a(a3), .b(b2), .out(multiplier_7_out));  // open: cin, cout
  Multiplier #(.width(32)) multiplier_8 (.a(a4), .b(b4), .out(multiplier_8_out));  // open: cin, cout
  Adder #(.width(32)) adder_1 (.a(multiplier_1_out), .b(multiplier_2_out), .out(out_9));  // open: cin, cout
  Adder #(.width(32)) adder_2 (.a(multiplier_3_out), .b(multiplier_4_out), .out(out_10));  // open: cin, cout
  Adder #(.width(32)) adder_3 (.a(multiplier_5_out), .b(multiplier_6_out), .out(out_11));  // open: cin, cout
  Adder #(.width(32)) adder_4 (.a(multiplier_7_out), .b(multiplier_8_out), .out(out_12));  // open: cin, cout
endmodule
