// Logisim project Fibonacci.circ as structural Verilog: 5 circuits, main circuit S0
module S0 (
  output out_1,
  output out_2,
  output out_3,
  output out_4
);

  wire clock_1_out, clock_2_out, not_1_out;
  wire [3:0] demultiplexer_1_out0, demultiplexer_1_out1, register_1_q, register_2_q, s1_1_o4;

  Clock clock_1 (.out(clock_1_out));
  S1 s1_1 (
    .I1(demultiplexer_1_out0[3]), .I2(demultiplexer_1_out0[2]), .I3(demultiplexer_1_out0[1]),
    .I4(demultiplexer_1_out0[0]), .O1(s1_1_o4[3]), .O2(s1_1_o4[2]), .O3(s1_1_o4[1]), .O4(s1_1_o4[0]));
  Register #(.width(4)) register_1 (.D(demultiplexer_1_out1), .Q(register_1_q), .clk(not_1_out));  // open: en, clr
  not not_1 (not_1_out, clock_1_out);
  Register #(.width(4)) register_2 (.D(s1_1_o4), .Q(register_2_q), .clk(clock_2_out));  // open: en, clr
  Clock clock_2 (.out(clock_2_out));
  Demultiplexer #(.width(4)) demultiplexer_1 (
    .out0(demultiplexer_1_out0), .out1(demultiplexer_1_out1), .in({out_1, out_2, out_3, out_4}),
    .sel(clock_2_out));  // open: en
  Adder #(.width(4)) adder_1 (
    .a(register_1_q), .b(register_2_q), .out({out_1, out_2, out_3, out_4}));  // open: cin, cout
  // Probe on {out_1, out_2, out_3, out_4}
endmodule

module main (
  input  [2:0] in_1,
  output [3:0] out_2
);

  wire comparator_1_eq;
  wire [3:0] s0_1_out_4, s2_1_o4;

  S2 s2_1 (
    .I1(in_1[2]), .I2(in_1[1]), .I3(in_1[0]), .O1(s2_1_o4[3]), .O2(s2_1_o4[2]), .O3(s2_1_o4[1]),
    .O4(s2_1_o4[0]));
  S0 s0_1 (.out_1(s0_1_out_4[3]), .out_2(s0_1_out_4[2]), .out_3(s0_1_out_4[1]), .out_4(s0_1_out_4[0]));
  Comparator #(.width(4), .mode("unsigned")) comparator_1 (
    .a(s2_1_o4), .b(s0_1_out_4), .eq(comparator_1_eq));  // open: gt, lt
  Register #(.width(4)) register_1 (.D(s0_1_out_4), .Q(out_2), .clk(comparator_1_eq));  // open: en, clr
endmodule

module S1 (
  input  I1,
  input  I2,
  input  I3,
  input  I4,
  output O1,
  output O2,
  output O3,
  output O4
);

  wire and_1_out, not_1_out, not_2_out, not_3_out;

  not not_1 (not_1_out, I1);
  not not_2 (not_2_out, I2);
  and and_1 (and_1_out, not_1_out, not_2_out, not_3_out);
  not not_3 (not_3_out, I3);
  or or_1 (O4, and_1_out, I4);

  assign O1 = I1;
  assign O2 = I2;
  assign O3 = I3;
endmodule

module S2 (
  input  I1,
  input  I2,
  input  I3,
  output O1,
  output O2,
  output O3,
  output O4
);

  wire and_3_out, and_4_out, and_5_out, and_6_out, and_7_out, and_8_out, not_1_out, not_2_out, not_3_out,
       not_4_out, not_5_out, not_6_out, not_7_out;

  and and_1 (O1, I1, I2);
  and and_2 (O2, I1, I3);
  not not_1 (not_1_out, I1);
  not not_2 (not_2_out, I2);
  not not_3 (not_3_out, I3);
  not not_4 (not_4_out, I2);
  not not_5 (not_5_out, I1);
  not not_6 (not_6_out, I3);
  not not_7 (not_7_out, I2);
  and and_3 (and_3_out, not_1_out, I2, I3);
  and and_4 (and_4_out, I1, not_2_out, not_3_out);
  and and_5 (and_5_out, not_4_out, I3);
  and and_6 (and_6_out, not_5_out, I2, not_6_out);
  and and_7 (and_7_out, I1, not_7_out);
  and and_8 (and_8_out, I1, I3);
  or or_1 (O3, and_3_out, and_4_out);
  or or_2 (O4, and_5_out, and_6_out, and_7_out, and_8_out);
endmodule

module Test (
  output [3:0] out_1,
  output out_2
);

  wire clock_1_out;
  wire [3:0] main_1_out_2;

  Clock clock_1 (.out(clock_1_out));
  main main_1 (.in_1(3'b111), .out_2(main_1_out_2));
  Register #(.width(4)) register_1 (.D(main_1_out_2), .Q(out_1), .clk(out_2));  // open: en, clr
  Counter #(.width(3), .max('h7)) counter_1 (.carry(out_2), .clk(clock_1_out));  // open: load, D, count, Q, clr
endmodule
