// Logisim project GRD.circ as structural Verilog: 1 circuit, main circuit grf
module grf (
  input  Clk,
  input  Reset,
  input  WE,
  input  [4:0] A1,
  input  [4:0] A2,
  input  [4:0] A3,
  input  [31:0] WD,
  output [31:0] RD1,
  output [31:0] RD2
);

  wire decoder_1_out0, En1, En2, En3, En4, En5, En6, En7, En8, En9, En10, En11, En12, En13, En14, En15, En16,
       En17, En18, En19, En20, En21, En22, En23, En24, En25, En26, En27, En28, En29, En30, En31;
  wire [31:0] O1, O2, O3, O4, O5, O6, O7, O8, O9, O10, O11, O12, O13, O14, O15, O16, O17, O18, O19, O20, O21,
       O22, O23, O24, O25, O26, O27, O28, O29, O30, O31;

  Register #(.width(32)) register_1 (.D(WD), .en(En1), .Q(O1), .clk(Clk), .clr(Reset));
  Register #(.width(32)) register_2 (.D(WD), .en(En9), .Q(O9), .clk(Clk), .clr(Reset));
  Register #(.width(32)) register_3 (.D(WD), .en(En17), .Q(O17), .clk(Clk), .clr(Reset));
  Register #(.width(32)) register_4 (.D(WD), .en(En25), .Q(O25), .clk(Clk), .clr(Reset));
  Register #(.width(32)) register_5 (.D(WD), .en(En2), .Q(O2), .clk(Clk), .clr(Reset));
  Register #(.width(32)) register_6 (.D(WD), .en(En10), .Q(O10), .clk(Clk), .clr(Reset));
  Register #(.width(32)) register_7 (.D(WD), .en(En18), .Q(O18), .clk(Clk), .clr(Reset));
  Register #(.width(32)) register_8 (.D(WD), .en(En26), .Q(O26), .clk(Clk), .clr(Reset));
  Register #(.width(32)) register_9 (.D(WD), .en(En3), .Q(O3), .clk(Clk), .clr(Reset));
  Register #(.width(32)) register_10 (.D(WD), .en(En11), .Q(O11), .clk(Clk), .clr(Reset));
  Register #(.width(32)) register_11 (.D(WD), .en(En19), .Q(O19), .clk(Clk), .clr(Reset));
  Register #(.width(32)) register_12 (.D(WD), .en(En27), .Q(O27), .clk(Clk), .clr(Reset));
  Register #(.width(32)) register_13 (.D(WD), .en(En4), .Q(O4), .clk(Clk), .clr(Reset));
  Register #(.width(32)) register_14 (.D(WD), .en(En5), .Q(O5), .clk(Clk), .clr(Reset));
  Register #(.width(32)) register_15 (.D(WD), .en(En13), .Q(O13), .clk(Clk), .clr(Reset));
  Register #(.width(32)) register_16 (.D(WD), .en(En12), .Q(O12), .clk(Clk), .clr(Reset));
  Register #(.width(32)) register_17 (.D(WD), .en(En21), .Q(O21), .clk(Clk), .clr(Reset));
  Register #(.width(32)) register_18 (.D(WD), .en(En20), .Q(O20), .clk(Clk), .clr(Reset));
  Register #(.width(32)) register_19 (.D(WD), .en(En29), .Q(O29), .clk(Clk), .clr(Reset));
  Register #(.width(32)) register_20 (.D(WD), .en(En28), .Q(O28), .clk(Clk), .clr(Reset));
  Register #(.width(32)) register_21 (.D(WD), .en(En6), .Q(O6), .clk(Clk), .clr(Reset));
  Register #(.width(32)) register_22 (.D(WD), .en(En14), .Q(O14), .clk(Clk), .clr(Reset));
  Register #(.width(32)) register_23 (.D(WD), .en(En22), .Q(O22), .clk(Clk), .clr(Reset));
  Register #(.width(32)) register_24 (.D(WD), .en(En30), .Q(O30), .clk(Clk), .clr(Reset));
  Register #(.width(32)) register_25 (.D(WD), .en(En7), .Q(O7), .clk(Clk), .clr(Reset));
  Register #(.width(32)) register_26 (.D(WD), .en(En15), .Q(O15), .clk(Clk), .clr(Reset));
  Register #(.width(32)) register_27 (.D(WD), .en(En23), .Q(O23), .clk(Clk), .clr(Reset));
  Register #(.width(32)) register_28 (.D(WD), .en(En31), .Q(O31), .clk(Clk), .clr(Reset));
  Register #(.width(32)) register_29 (.D(WD), .en(En8), .Q(O8), .clk(Clk), .clr(Reset));
  Register #(.width(32)) register_30 (.D(WD), .en(En16), .Q(O16), .clk(Clk), .clr(Reset));
  Register #(.width(32)) register_31 (.D(WD), .en(En24), .Q(O24), .clk(Clk), .clr(Reset));
  Multiplexer #(.select(5), .width(32)) multiplexer_1 (
    .in0({32{1'b0}}), .in1(O1), .in2(O2), .in3(O3), .in4(O4), .in5(O5), .in6(O6), .in7(O7), .in8(O8),
    .in9(O9), .in10(O10), .in11(O11), .in12(O12), .in13(O13), .in14(O14), .in15(O15), .in16(O16), .in17(O17),
    .in18(O18), .in19(O19), .in20(O20), .in21(O21), .in22(O22), .in23(O23), .in24(O24), .in25(O25),
    .in26(O26), .in27(O27), .in28(O28), .in29(O29), .in30(O30), .in31(O31), .out(RD1), .sel(A1));  // open: en
  Multiplexer #(.select(5), .width(32)) multiplexer_2 (
    .in0({32{1'b0}}), .in1(O1), .in2(O2), .in3(O3), .in4(O4), .in5(O5), .in6(O6), .in7(O7), .in8(O8),
    .in9(O9), .in10(O10), .in11(O11), .in12(O12), .in13(O13), .in14(O14), .in15(O15), .in16(O16), .in17(O17),
    .in18(O18), .in19(O19), .in20(O20), .in21(O21), .in22(O22), .in23(O23), .in24(O24), .in25(O25),
    .in26(O26), .in27(O27), .in28(O28), .in29(O29), .in30(O30), .in31(O31), .out(RD2), .sel(A2));  // open: en
  Decoder #(.select(5), .disabled(0)) decoder_1 (
    .out0(decoder_1_out0), .out1(En1), .out2(En2), .out3(En3), .out4(En4), .out5(En5), .out6(En6),
    .out7(En7), .out8(En8), .out9(En9), .out10(En10), .out11(En11), .out12(En12), .out13(En13), .out14(En14),
    .out15(En15), .out16(En16), .out17(En17), .out18(En18), .out19(En19), .out20(En20), .out21(En21),
    .out22(En22), .out23(En23), .out24(En24), .out25(En25), .out26(En26), .out27(En27), .out28(En28),
    .out29(En29), .out30(En30), .out31(En31), .sel(A3), .en(WE));

  // Other names for the same wires on the sheet: I1[31:0] = WD; I2[31:0] = WD; I3[31:0] = WD; I4[31:0] = WD;
  //   I5[31:0] = WD; I6[31:0] = WD; I7[31:0] = WD; I8[31:0] = WD; I9[31:0] = WD; I10[31:0] = WD; I11[31:0] = WD;
  //   I12[31:0] = WD; I13[31:0] = WD; I14[31:0] = WD; I15[31:0] = WD; I16[31:0] = WD; I17[31:0] = WD; I18[31:0] = WD;
  //   I19[31:0] = WD; I20[31:0] = WD; I21[31:0] = WD; I22[31:0] = WD; I23[31:0] = WD; I24[31:0] = WD; I25[31:0] = WD;
  //   I26[31:0] = WD; I27[31:0] = WD; I28[31:0] = WD; I29[31:0] = WD; I30[31:0] = WD; I31[31:0] = WD
endmodule
