// Logisim project ROM.circ as structural Verilog: 1 circuit, main circuit main
module main (
);

  wire [7:0] _0, _1, _2, _3, _10, _11, _12, _13, _20, _21, _22, _23, _30, _31, _32, _33, _40, _41, _42, _43,
       _50, _51, _52, _53, _60, _61, _62, _63, _70, _71, _72, _73, _80, _81, _82, _83, _90, _91, _92, _93,
       _100, _101, _102, _103, _110, _111, _112, _113, _120, _121, _122, _123, _130, _131, _132, _133, _140,
       _141, _142, _143, _150, _151, _152, _153;

  ROM rom_1 (.data(_0));  // open: addr, sel
  ROM rom_2 (.data(_10));  // open: addr, sel
  ROM rom_3 (.data(_20));  // open: addr, sel
  ROM rom_4 (.data(_30));  // open: addr, sel
  ROM rom_5 (.data(_40));  // open: addr, sel
  ROM rom_6 (.data(_50));  // open: addr, sel
  ROM rom_7 (.data(_60));  // open: addr, sel
  ROM rom_8 (.data(_70));  // open: addr, sel
  ROM rom_9 (.data(_80));  // open: addr, sel
  ROM rom_10 (.data(_90));  // open: addr, sel
  ROM rom_11 (.data(_100));  // open: addr, sel
  ROM rom_12 (.data(_110));  // open: addr, sel
  ROM rom_13 (.data(_120));  // open: addr, sel
  ROM rom_14 (.data(_130));  // open: addr, sel
  ROM rom_15 (.data(_140));  // open: addr, sel
  ROM rom_16 (.data(_150));  // open: addr, sel
  ROM rom_17 (.data(_1));  // open: addr, sel
  ROM rom_18 (.data(_11));  // open: addr, sel
  ROM rom_19 (.data(_21));  // open: addr, sel
  ROM rom_20 (.data(_31));  // open: addr, sel
  ROM rom_21 (.data(_41));  // open: addr, sel
  ROM rom_22 (.data(_51));  // open: addr, sel
  ROM rom_23 (.data(_61));  // open: addr, sel
  ROM rom_24 (.data(_71));  // open: addr, sel
  ROM rom_25 (.data(_81));  // open: addr, sel
  ROM rom_26 (.data(_91));  // open: addr, sel
  ROM rom_27 (.data(_101));  // open: addr, sel
  ROM rom_28 (.data(_111));  // open: addr, sel
  ROM rom_29 (.data(_121));  // open: addr, sel
  ROM rom_30 (.data(_131));  // open: addr, sel
  ROM rom_31 (.data(_141));  // open: addr, sel
  ROM rom_32 (.data(_151));  // open: addr, sel
  ROM rom_33 (.data(_2));  // open: addr, sel
  ROM rom_34 (.data(_12));  // open: addr, sel
  ROM rom_35 (.data(_22));  // open: addr, sel
  ROM rom_36 (.data(_32));  // open: addr, sel
  ROM rom_37 (.data(_42));  // open: addr, sel
  ROM rom_38 (.data(_52));  // open: addr, sel
  ROM rom_39 (.data(_62));  // open: addr, sel
  ROM rom_40 (.data(_72));  // open: addr, sel
  ROM rom_41 (.data(_82));  // open: addr, sel
  ROM rom_42 (.data(_92));  // open: addr, sel
  ROM rom_43 (.data(_102));  // open: addr, sel
  ROM rom_44 (.data(_112));  // open: addr, sel
  ROM rom_45 (.data(_122));  // open: addr, sel
  ROM rom_46 (.data(_132));  // open: addr, sel
  ROM rom_47 (.data(_142));  // open: addr, sel
  ROM rom_48 (.data(_152));  // open: addr, sel
  ROM rom_49 (.data(_3));  // open: addr, sel
  ROM rom_50 (.data(_13));  // open: addr, sel
  ROM rom_51 (.data(_23));  // open: addr, sel
  ROM rom_52 (.data(_33));  // open: addr, sel
  ROM rom_53 (.data(_43));  // open: addr, sel
  ROM rom_54 (.data(_53));  // open: addr, sel
  ROM rom_55 (.data(_63));  // open: addr, sel
  ROM rom_56 (.data(_73));  // open: addr, sel
  ROM rom_57 (.data(_83));  // open: addr, sel
  ROM rom_58 (.data(_93));  // open: addr, sel
  ROM rom_59 (.data(_103));  // open: addr, sel
  ROM rom_60 (.data(_113));  // open: addr, sel
  ROM rom_61 (.data(_123));  // open: addr, sel
  ROM rom_62 (.data(_133));  // open: addr, sel
  ROM rom_63 (.data(_143));  // open: addr, sel
  ROM rom_64 (.data(_153));  // open: addr, sel
endmodule
