// Logisim project compar2.circ as structural Verilog: 2 circuits, main circuit main
module main (
  input  [3:0] in_1,
  input  [3:0] in_2,
  output out_3
);

  wire and_1_out, and_2_out, and_3_out, n1_bit_1_o1, n1_bit_1_o2, n1_bit_2_o1, n1_bit_2_o2, n1_bit_3_o1,
       n1_bit_3_o2, n1_bit_4_o1, or_1_out, or_2_out, or_3_out;

  _1_bit u_1_bit_1 (.a(in_1[3]), .b(in_2[3]), .O1(n1_bit_1_o1), .O2(n1_bit_1_o2));  // open: O3
  _1_bit u_1_bit_2 (.a(in_1[2]), .b(in_2[2]), .O1(n1_bit_2_o1), .O2(n1_bit_2_o2));  // open: O3
  _1_bit u_1_bit_3 (.a(in_1[1]), .b(in_2[1]), .O1(n1_bit_3_o1), .O2(n1_bit_3_o2));  // open: O3
  _1_bit u_1_bit_4 (.a(in_1[0]), .b(in_2[0]), .O1(n1_bit_4_o1));  // open: O2, O3
  or or_1 (or_1_out, n1_bit_1_o1, n1_bit_1_o2);
  or or_2 (or_2_out, n1_bit_2_o1, n1_bit_2_o2);
  or or_3 (or_3_out, n1_bit_3_o1, n1_bit_3_o2);
  and and_1 (and_1_out, or_1_out, n1_bit_2_o1);
  and and_2 (and_2_out, or_1_out, or_2_out, n1_bit_3_o1);
  and and_3 (and_3_out, or_1_out, or_3_out, n1_bit_4_o1);
  or or_4 (out_3, n1_bit_1_o1, and_1_out, and_2_out, and_3_out);
endmodule

module _1_bit (
  input  a,
  input  b,
  output O1,
  output O2,
  output O3
);

  wire and_2_out, and_3_out, not_1_out, not_2_out, not_3_out, not_4_out;

  not not_1 (not_1_out, b);
  not not_2 (not_2_out, a);
  not not_3 (not_3_out, b);
  not not_4 (not_4_out, a);
  and and_1 (O1, a, not_1_out);
  and and_2 (and_2_out, not_2_out, not_3_out);
  and and_3 (and_3_out, a, b);
  and and_4 (O3, not_4_out, b);
  or or_1 (O2, and_2_out, and_3_out);
endmodule
