// Logisim project cou.circ as structural Verilog: 6 circuits, main circuit main
module main (
  input  Reset,
  output [31:0] out_2,
  output RegWrite,
  output [4:0] RegAddr,
  output [31:0] RegData,
  output out_6
);

  wire add, ALUsrc, beq, Clk, ExtOP, lw, nPC_sel, ori, RegDst, sub, sw;
  wire [1:0] ALUOp;
  wire [15:0] adder_1_out, PC;
  wire [31:0] RD1, RD2, RegIn, RegOut;

  Clock clock_1 (.out(Clk));
  // Probe on ori
  Adder #(.width(16)) adder_1 (.a(PC), .b(16'h1), .out(adder_1_out));  // open: cin, cout
  // Probe on add
  // Probe on sub
  ROM #(.addrWidth(16), .dataWidth(32)) rom_1 (.addr(PC), .data(out_2));  // open: sel
  Register #(.width(16)) register_1 (.D(adder_1_out), .Q(PC), .clk(Clk));  // open: en, clr
  // Probe on sw
  // Probe on lw
  // Probe on beq
  RAM #(.addrWidth(5), .dataWidth(32), .bus("separate")) ram_1 (
    .addr(out_2[15:11]), .din(RegOut), .data(RegIn), .str(out_6), .ld(RegWrite), .clr(Reset));  // open: sel, clk
  orand orand_1 (
    .in_1(out_2[31:26]), .RegDst(RegDst), .ALUSrc(ALUsrc), .Regwrite(RegWrite), .Memwrite(out_6),
    .nPC_sel(nPC_sel), .ExtOp(ExtOP), .ALUOp(ALUOp), .ori(ori), .add(add), .sub(sub), .lw(lw), .sw(sw),
    .beq(beq));
  Reg reg_1 (
    .in_4(out_2[25:21]), .in_5(out_2[20:16]), .in_6(out_2[15:11]), .WD3(RegData), .Clk(Clk), .WE3(RegWrite),
    .Reset(Reset), .out_8(RD1), .out_9(RD2));
  ALU alu_1 (.in_3(RD1), .in_4(RD2), .ALUResult(RegData), .ALUOp(ALUOp), .func(out_2[5:0]));

  assign RegAddr = out_2[15:11];

  // Other names for the same wires on the sheet: _6_10[4:0] = out_2[10:6]; address[25:0] = out_2[31:6];
  //   immediate[15:0] = out_2[15:0]; Instr[31:0] = out_2; shamt[4:0] = out_2[10:6]; _11_15[4:0] = out_2[15:11];
  //   rd[4:0] = out_2[15:11]; _16_20[4:0] = out_2[20:16]; rt[4:0] = out_2[20:16]; _21_25[4:0] = out_2[25:21];
  //   rs[4:0] = out_2[25:21]; _26_31[5:0] = out_2[31:26]; op[5:0] = out_2[31:26]; _0_5[5:0] = out_2[5:0];
  //   func[5:0] = out_2[5:0]; MemWrite = out_6; WD3[31:0] = RegData

  // Notes on the sheet:
  //   contents of rom_1 (hex, n*v repeats v):
  //   341c0000 341d0000 340080f8 36ee0367 3593769c 34dda539 3465c5dc 34be0ff1 3472af1d 35566602 35fe72a7
  //   3437ff23 37b9649e 3690bf9b 37fe4e0c 3711f49d 3c113bfe 3c057433 3c03c451 3c04c431 3c1c24d9 3c1bf0da
  //   3c0ccc68 3c0a118d 3c1021ea 3c0004d3 3c16115b 3c184f06 3c1215de 1000ffff
endmodule

module orand (
  input  [5:0] in_1,
  output ori,
  output add,
  output sub,
  output lw,
  output sw,
  output beq,
  output RegDst,
  output ALUSrc,
  output Regwrite,
  output Memwrite,
  output nPC_sel,
  output ExtOp,
  output [1:0] ALUOp
);

  wire if_1, if_3, not_1_out, not_2_out, not_3_out, not_4_out, not_5_out, not_6_out;

  not not_1 (not_1_out, in_1[5]);
  not not_2 (not_2_out, in_1[4]);
  not not_3 (not_3_out, in_1[2]);
  not not_4 (not_4_out, in_1[3]);
  not not_5 (not_5_out, in_1[1]);
  not not_6 (not_6_out, in_1[0]);
  and u_ori (ori, not_1_out, not_2_out, in_1[3], in_1[2], not_5_out, in_1[0]);
  and u_add (add, not_1_out, not_2_out, not_4_out, not_3_out, not_5_out, not_6_out);
  and u_sub (sub, not_1_out, not_2_out, not_4_out, not_3_out, not_5_out, not_6_out);
  and u_lw (lw, in_1[5], not_2_out, not_4_out, not_3_out, in_1[1], in_1[0]);
  and u_sw (Memwrite, in_1[5], not_2_out, in_1[3], not_3_out, in_1[1], in_1[0]);
  and u_beq (beq, not_1_out, not_2_out, not_4_out, in_1[2], not_5_out, not_6_out);
  or u_RegDst (RegDst, add, sub);
  or u_ALUSrc (ALUSrc, ori, lw);
  or u_Regwrite (Regwrite, add, sub, ori, lw);
  or u_ExtOp (ExtOp, lw, Memwrite);
  or u_if_1 (if_1, ori, add, sub);
  or if_2 (if_3, lw, Memwrite);
  model1 model1_1 (.I1(if_1), .I2(beq), .I3(if_3), .OP1(ALUOp[0]), .OP2(ALUOp[1]));

  assign nPC_sel = beq;
  assign sw = Memwrite;

  // Other names for the same wires on the sheet: if_2 = beq; op0 = in_1[0]; op1 = in_1[1]; op2 = in_1[2];
  //   op3 = in_1[3]; op4 = in_1[4]; op5 = in_1[5]
endmodule

module ALU (
  input  [1:0] ALUOp,
  input  [5:0] func,
  input  [31:0] in_3,
  input  [31:0] in_4,
  output [31:0] ALUResult
);

  wire [2:0] model2_1_o3;
  wire [31:0] ADDU, AND, ORI, SUBU, temp;

  model2 model2_1 (
    .F3(func[5]), .F4(func[4]), .F5(func[3]), .F6(func[2]), .O1(model2_1_o3[2]), .O2(model2_1_o3[1]),
    .O3(model2_1_o3[0]));
  Multiplexer #(.select(3), .width(32), .disabled(0), .enable("false")) multiplexer_1 (
    .in0(AND), .in1(ORI), .in2(ADDU), .in6(SUBU), .out(temp), .sel(model2_1_o3));  // open: in3, in4, in5, in7
  Multiplexer #(.select(2), .width(32), .enable("false")) multiplexer_2 (
    .in0(ADDU), .in1(SUBU), .in2(temp), .in3(temp), .out(ALUResult), .sel(ALUOp));
  Adder #(.width(32)) adder_1 (.a(in_3), .b(in_4), .out(ADDU));  // open: cin, cout
  Subtractor #(.width(32)) subtractor_1 (.a(in_3), .b(in_4), .out(SUBU));  // open: bin, bout
  assign ORI = in_3 | in_4;  // OR_Gate or_1, 32 bits wide
  assign AND = in_3 & in_4;  // AND_Gate and_1, 32 bits wide

  // Other names for the same wires on the sheet: IN1[31:0] = in_3; IN2[31:0] = in_4
endmodule

module Reg (
  input  Clk,
  input  WE3,
  input  Reset,
  input  [4:0] in_4,
  input  [4:0] in_5,
  input  [4:0] in_6,
  input  [31:0] WD3,
  output [31:0] out_8,
  output [31:0] out_9
);

  wire Regwrite1, Regwrite2, Regwrite3, Regwrite4, Regwrite5, Regwrite6, Regwrite7, Regwrite8, Regwrite9,
       Regwrite10, Regwrite11, Regwrite12, Regwrite13, Regwrite14, Regwrite15, Regwrite16, Regwrite17,
       Regwrite18, Regwrite19, Regwrite20, Regwrite21, Regwrite22, Regwrite23, Regwrite24, Regwrite25,
       Regwrite26, Regwrite27, Regwrite28, Regwrite29, Regwrite30, Regwrite31;
  wire [31:0] RegOut0, RegOut1, RegOut2, RegOut3, RegOut4, RegOut5, RegOut6, RegOut7, RegOut8, RegOut9,
       RegOut10, RegOut11, RegOut12, RegOut13, RegOut14, RegOut15, RegOut16, RegOut17, RegOut18, RegOut19,
       RegOut20, RegOut21, RegOut22, RegOut23, RegOut24, RegOut25, RegOut26, RegOut27, RegOut28, RegOut29,
       RegOut30, RegOut31;

  Multiplexer #(.select(5), .width(32), .enable("false")) multiplexer_1 (
    .in0(RegOut0), .in1(RegOut1), .in2(RegOut2), .in3(RegOut3), .in4(RegOut4), .in5(RegOut5), .in6(RegOut6),
    .in7(RegOut7), .in8(RegOut8), .in9(RegOut9), .in10(RegOut10), .in11(RegOut11), .in12(RegOut12),
    .in13(RegOut13), .in14(RegOut14), .in15(RegOut15), .in16(RegOut16), .in17(RegOut17), .in18(RegOut18),
    .in19(RegOut19), .in20(RegOut20), .in21(RegOut21), .in22(RegOut22), .in23(RegOut23), .in24(RegOut24),
    .in25(RegOut25), .in26(RegOut26), .in27(RegOut27), .in28(RegOut28), .in29(RegOut29), .in30(RegOut30),
    .in31(RegOut31), .out(out_8), .sel(in_4));
  Multiplexer #(.select(5), .width(32), .enable("false")) multiplexer_2 (
    .in0(RegOut0), .in1(RegOut1), .in2(RegOut2), .in3(RegOut3), .in4(RegOut4), .in5(RegOut5), .in6(RegOut6),
    .in7(RegOut7), .in8(RegOut8), .in9(RegOut9), .in10(RegOut10), .in11(RegOut11), .in12(RegOut12),
    .in13(RegOut13), .in14(RegOut14), .in15(RegOut15), .in16(RegOut16), .in17(RegOut17), .in18(RegOut18),
    .in19(RegOut19), .in20(RegOut20), .in21(RegOut21), .in22(RegOut22), .in23(RegOut23), .in24(RegOut24),
    .in25(RegOut25), .in26(RegOut26), .in27(RegOut27), .in28(RegOut28), .in29(RegOut29), .in30(RegOut30),
    .in31(RegOut31), .out(out_9), .sel(in_5));
  Decoder #(.select(5), .disabled(0)) decoder_1 (
    .out1(Regwrite1), .out2(Regwrite2), .out3(Regwrite3), .out4(Regwrite4), .out5(Regwrite5),
    .out6(Regwrite6), .out7(Regwrite7), .out8(Regwrite8), .out9(Regwrite9), .out10(Regwrite10),
    .out11(Regwrite11), .out12(Regwrite12), .out13(Regwrite13), .out14(Regwrite14), .out15(Regwrite15),
    .out16(Regwrite16), .out17(Regwrite17), .out18(Regwrite18), .out19(Regwrite19), .out20(Regwrite20),
    .out21(Regwrite21), .out22(Regwrite22), .out23(Regwrite23), .out24(Regwrite24), .out25(Regwrite25),
    .out26(Regwrite26), .out27(Regwrite27), .out28(Regwrite28), .out29(Regwrite29), .out30(Regwrite30),
    .out31(Regwrite31), .sel(in_6), .en(WE3));  // open: out0
  Register #(.width(32)) register_1 (.D({32{1'b0}}), .Q(RegOut0), .clk(Clk), .clr(Reset));  // open: en
  Register #(.width(32)) register_2 (.D(WD3), .en(Regwrite4), .Q(RegOut4), .clk(Clk), .clr(Reset));
  Register #(.width(32)) register_3 (.D(WD3), .en(Regwrite8), .Q(RegOut8), .clk(Clk), .clr(Reset));
  Register #(.width(32)) register_4 (.D(WD3), .en(Regwrite12), .Q(RegOut12), .clk(Clk), .clr(Reset));
  Register #(.width(32)) register_5 (.D(WD3), .en(Regwrite16), .Q(RegOut16), .clk(Clk), .clr(Reset));
  Register #(.width(32)) register_6 (.D(WD3), .en(Regwrite20), .Q(RegOut20), .clk(Clk), .clr(Reset));
  Register #(.width(32)) register_7 (.D(WD3), .en(Regwrite24), .Q(RegOut24), .clk(Clk), .clr(Reset));
  Register #(.width(32)) register_8 (.D(WD3), .en(Regwrite28), .Q(RegOut28), .clk(Clk), .clr(Reset));
  Register #(.width(32)) register_9 (.D(WD3), .en(Regwrite1), .Q(RegOut1), .clk(Clk), .clr(Reset));
  Register #(.width(32)) register_10 (.D(WD3), .en(Regwrite5), .Q(RegOut5), .clk(Clk), .clr(Reset));
  Register #(.width(32)) register_11 (.D(WD3), .en(Regwrite9), .Q(RegOut9), .clk(Clk), .clr(Reset));
  Register #(.width(32)) register_12 (.D(WD3), .en(Regwrite13), .Q(RegOut13), .clk(Clk), .clr(Reset));
  Register #(.width(32)) register_13 (.D(WD3), .en(Regwrite17), .Q(RegOut17), .clk(Clk), .clr(Reset));
  Register #(.width(32)) register_14 (.D(WD3), .en(Regwrite21), .Q(RegOut21), .clk(Clk), .clr(Reset));
  Register #(.width(32)) register_15 (.D(WD3), .en(Regwrite25), .Q(RegOut25), .clk(Clk), .clr(Reset));
  Register #(.width(32)) register_16 (.D(WD3), .en(Regwrite29), .Q(RegOut29), .clk(Clk), .clr(Reset));
  Register #(.width(32)) register_17 (.D(WD3), .en(Regwrite2), .Q(RegOut2), .clk(Clk), .clr(Reset));
  Register #(.width(32)) register_18 (.D(WD3), .en(Regwrite6), .Q(RegOut6), .clk(Clk), .clr(Reset));
  Register #(.width(32)) register_19 (.D(WD3), .en(Regwrite10), .Q(RegOut10), .clk(Clk), .clr(Reset));
  Register #(.width(32)) register_20 (.D(WD3), .en(Regwrite14), .Q(RegOut14), .clk(Clk), .clr(Reset));
  Register #(.width(32)) register_21 (.D(WD3), .en(Regwrite18), .Q(RegOut18), .clk(Clk), .clr(Reset));
  Register #(.width(32)) register_22 (.D(WD3), .en(Regwrite22), .Q(RegOut22), .clk(Clk), .clr(Reset));
  Register #(.width(32)) register_23 (.D(WD3), .en(Regwrite26), .Q(RegOut26), .clk(Clk), .clr(Reset));
  Register #(.width(32)) register_24 (.D(WD3), .en(Regwrite30), .Q(RegOut30), .clk(Clk), .clr(Reset));
  Register #(.width(32)) register_25 (.D(WD3), .en(Regwrite3), .Q(RegOut3), .clk(Clk), .clr(Reset));
  Register #(.width(32)) register_26 (.D(WD3), .en(Regwrite7), .Q(RegOut7), .clk(Clk), .clr(Reset));
  Register #(.width(32)) register_27 (.D(WD3), .en(Regwrite11), .Q(RegOut11), .clk(Clk), .clr(Reset));
  Register #(.width(32)) register_28 (.D(WD3), .en(Regwrite15), .Q(RegOut15), .clk(Clk), .clr(Reset));
  Register #(.width(32)) register_29 (.D(WD3), .en(Regwrite19), .Q(RegOut19), .clk(Clk), .clr(Reset));
  Register #(.width(32)) register_30 (.D(WD3), .en(Regwrite23), .Q(RegOut23), .clk(Clk), .clr(Reset));
  Register #(.width(32)) register_31 (.D(WD3), .en(Regwrite27), .Q(RegOut27), .clk(Clk), .clr(Reset));
  Register #(.width(32)) register_32 (.D(WD3), .en(Regwrite31), .Q(RegOut31), .clk(Clk), .clr(Reset));

  // Other names for the same wires on the sheet: A1[4:0] = in_4; A2[4:0] = in_5; A3[4:0] = in_6; Clr = Reset;
  //   RD1[31:0] = out_8; RD2[31:0] = out_9; RegIn[31:0] = WD3; Regwrite = WE3
endmodule

module model1 (
  input  I1,
  input  I2,
  input  I3,
  output OP1,
  output OP2
);

  wire and_1_out, and_2_out, and_3_out, and_4_out, not_1_out, not_2_out, not_3_out, not_4_out, or_1_out,
       or_2_out;

  not not_1 (not_1_out, I1);
  not not_2 (not_2_out, I2);
  not not_3 (not_3_out, I1);
  not not_4 (not_4_out, I3);
  and and_1 (and_1_out, not_1_out, not_2_out);
  and and_2 (and_2_out, not_3_out, not_4_out);
  or or_1 (or_1_out, and_1_out, I3);
  and and_3 (and_3_out, I1, I2);
  or or_2 (or_2_out, and_2_out, I2);
  and and_4 (and_4_out, I1, I3);
  or or_3 (OP1, or_1_out, and_3_out);
  or or_4 (OP2, or_2_out, and_4_out);
endmodule

module model2 (
  input  F3,
  input  F4,
  input  F5,
  input  F6,
  output O1,
  output O2,
  output O3
);

  not not_1 (O2, F4);
  or or_1 (O3, F6, F3);

  assign O1 = F5;
endmodule
