// Logisim project fsm.circ as structural Verilog: 1 circuit, main circuit fsm
module fsm (
  input  in_1,
  input  [1:0] in_2,
  output out_3
);

  wire clock_1_out, register_2_q;
  wire [1:0] multiplexer_1_out, register_1_q;

  Clock clock_1 (.out(clock_1_out));
  Register #(.width(2)) register_1 (
    .D(multiplexer_1_out), .Q(register_1_q), .clk(clock_1_out), .clr(register_2_q));  // open: en
  Register #(.width(1)) register_2 (.D(in_1), .Q(register_2_q), .clk(clock_1_out), .clr(register_2_q));  // open: en
  Multiplexer #(.select(4), .width(2)) multiplexer_1 (
    .in0(2'b00), .in1(2'b01), .in2(2'b00), .in3(2'b00), .in4(2'b10), .in5(2'b01), .in6(2'b10), .in7(2'b00),
    .in8(2'b11), .in9(2'b01), .in10(2'b11), .in11(2'b00), .in12(2'b00), .in13(2'b01), .in14(2'b00),
    .in15(2'b00), .out(multiplexer_1_out), .sel({register_1_q, in_2}));  // open: en
  Multiplexer #(.select(2)) multiplexer_2 (
    .in0(1'b0), .in1(1'b0), .in2(1'b0), .in3(1'b1), .out(out_3), .sel(multiplexer_1_out));  // open: en
endmodule
