// Logisim project swap.circ as structural Verilog: 3 circuits, main circuit 1bit_swap
module _1bit_swap (
  input  l1,
  input  l2,
  input  s,
  output O1,
  output O2
);

  wire and_1_out, and_2_out, and_3_out, and_4_out, not_1_out, not_2_out;

  not not_1 (not_1_out, s);
  not not_2 (not_2_out, s);
  and and_1 (and_1_out, l2, s);
  and and_2 (and_2_out, l1, not_1_out);
  and and_3 (and_3_out, l2, not_2_out);
  and and_4 (and_4_out, l1, s);
  or or_1 (O1, and_1_out, and_2_out);
  or or_2 (O2, and_3_out, and_4_out);
endmodule

module _4bit_swap (
  input  [3:0] A,
  input  [3:0] B,
  input  S,
  output [3:0] C,
  output [3:0] D
);

  _1bit_swap u_1bit_swap_1 (.l1(A[0]), .l2(B[0]), .s(S), .O1(C[0]), .O2(D[0]));
  _1bit_swap u_1bit_swap_2 (.l1(A[1]), .l2(B[1]), .s(S), .O1(C[1]), .O2(D[1]));
  _1bit_swap u_1bit_swap_3 (.l1(A[2]), .l2(B[2]), .s(S), .O1(C[2]), .O2(D[2]));
  _1bit_swap u_1bit_swap_4 (.l1(A[3]), .l2(B[3]), .s(S), .O1(C[3]), .O2(D[3]));
endmodule

module _4bit_sort (
  input  [3:0] A,
  input  [3:0] B,
  input  [3:0] C,
  input  [3:0] D,
  output [3:0] out_5,
  output [3:0] out_6,
  output [3:0] out_7,
  output [3:0] out_8
);

  wire comparator_1_gt, comparator_2_gt, comparator_3_eq, comparator_3_gt, comparator_4_gt, comparator_5_eq,
       comparator_5_gt;
  wire [3:0] n4bit_swap_1_c, n4bit_swap_1_d, n4bit_swap_2_c, n4bit_swap_2_d, n4bit_swap_3_d, n4bit_swap_4_c;

  Comparator #(.width(4), .mode("unsigned")) comparator_1 (.a(A), .b(B), .gt(comparator_1_gt));  // open: eq, lt
  Comparator #(.width(4), .mode("unsigned")) comparator_2 (.a(C), .b(D), .gt(comparator_2_gt));  // open: eq, lt
  _4bit_swap u_4bit_swap_1 (.A(A), .B(B), .S(comparator_1_gt), .C(n4bit_swap_1_c), .D(n4bit_swap_1_d));
  _4bit_swap u_4bit_swap_2 (.A(C), .B(D), .S(comparator_2_gt), .C(n4bit_swap_2_c), .D(n4bit_swap_2_d));
  Comparator #(.width(4), .mode("unsigned")) comparator_3 (
    .a(n4bit_swap_1_c), .b(n4bit_swap_2_c), .gt(comparator_3_gt), .eq(comparator_3_eq), .lt(comparator_3_eq));
  Comparator #(.width(4), .mode("unsigned")) comparator_4 (
    .a(n4bit_swap_1_d), .b(n4bit_swap_2_d), .gt(comparator_4_gt));  // open: eq, lt
  _4bit_swap u_4bit_swap_3 (.A(n4bit_swap_1_c), .B(n4bit_swap_2_c), .S(comparator_3_gt), .C(out_5), .D(n4bit_swap_3_d));
  _4bit_swap u_4bit_swap_4 (.A(n4bit_swap_1_d), .B(n4bit_swap_2_d), .S(comparator_4_gt), .C(n4bit_swap_4_c), .D(out_8));
  Comparator #(.width(4), .mode("unsigned")) comparator_5 (
    .a(n4bit_swap_3_d), .b(n4bit_swap_4_c), .gt(comparator_5_gt), .eq(comparator_5_eq), .lt(comparator_5_eq));
  _4bit_swap u_4bit_swap_5 (.A(n4bit_swap_3_d), .B(n4bit_swap_4_c), .S(comparator_5_gt), .C(out_6), .D(out_7));
endmodule
