// Logisim project 竞赛.circ as structural Verilog: 1 circuit, main circuit main
module main (
);

  wire _1, _2, _3, _4, button_1_out, button_2_out, button_3_out, button_4_out, d_ff_1_q, d_ff_2_q, d_ff_3_q,
       d_ff_4_q, EN, In;

  Button button_1 (.out(button_1_out));
  Button button_2 (.out(button_2_out));
  Button button_3 (.out(button_3_out));
  Button button_4 (.out(button_4_out));
  Button button_5 (.out(In));
  D_Flip_Flop d_ff_1 (.clk(button_1_out), .D(1'b1), .Q(d_ff_1_q), .Qn(_1), .en(EN), .reset(In));  // open: preset
  D_Flip_Flop d_ff_2 (.clk(button_2_out), .D(1'b1), .Q(d_ff_2_q), .Qn(_2), .en(EN), .reset(In));  // open: preset
  D_Flip_Flop d_ff_3 (.clk(button_3_out), .D(1'b1), .Q(d_ff_3_q), .Qn(_3), .en(EN), .reset(In));  // open: preset
  D_Flip_Flop d_ff_4 (.clk(button_4_out), .D(1'b1), .Q(d_ff_4_q), .Qn(_4), .en(EN), .reset(In));  // open: preset
  and and_1 (EN, _1, _2, _3, _4);
  LED led_1 (.in(d_ff_1_q));
  LED led_2 (.in(d_ff_2_q));
  LED led_3 (.in(d_ff_3_q));
  LED led_4 (.in(d_ff_4_q));
endmodule
