// Logisim project 等价电路.circ as structural Verilog: 3 circuits, main circuit main
module main (
  input  A,
  input  B,
  input  C,
  output Y
);

  wire and_1_out, and_2_out, and_3_out, and_4_out, not_1_out, not_2_out, not_3_out, not_4_out;

  not not_1 (not_1_out, C);
  not not_2 (not_2_out, B);
  not not_3 (not_3_out, C);
  not not_4 (not_4_out, A);
  and and_1 (and_1_out, not_1_out, not_2_out, A);
  and and_2 (and_2_out, not_3_out, B, A);
  and and_3 (and_3_out, C, B, not_4_out);
  and and_4 (and_4_out, C, B, A);
  or or_1 (Y, and_1_out, and_2_out, and_3_out, and_4_out);
endmodule

module C (
  input  A,
  input  B,
  input  C,
  output Y
);

  wire and_1_out, and_2_out, not_1_out, not_2_out, not_3_out, not_4_out, not_5_out, not_6_out, or_1_out,
       or_2_out;

  not not_1 (not_1_out, A);
  not not_2 (not_2_out, B);
  not not_3 (not_3_out, A);
  not not_4 (not_4_out, A);
  or or_1 (or_1_out, C, B, not_1_out);
  or or_2 (or_2_out, C, not_2_out, not_3_out);
  and and_1 (and_1_out, C, B, not_4_out);
  and and_2 (and_2_out, C, B, A);
  not not_5 (not_5_out, or_1_out);
  not not_6 (not_6_out, or_2_out);
  or or_3 (Y, not_5_out, not_6_out, and_1_out, and_2_out);
endmodule

module D (
  input  A,
  input  B,
  input  C,
  output out_4
);

  wire not_1_out, or_1_out, or_2_out;

  or or_1 (or_1_out, A, C);
  or or_2 (or_2_out, B, not_1_out);
  not not_1 (not_1_out, C);
  and and_1 (out_4, or_1_out, or_2_out);
endmodule
