// Logisim project 2mod5.circ as structural Verilog: 5 circuits, main circuit S1
module S1 (
  input  in_1,
  output out_2,
  output out_3,
  output out_4
);

  wire clock_1_out;
  wire [2:0] register_1_q;

  Register #(.width(3), .trigger("high")) register_1 (
    .D({out_2, out_3, out_4}), .Q(register_1_q), .clk(clock_1_out));  // open: en, clr
  Clock clock_1 (.out(clock_1_out));
  S0 s0_1 (
    .In_1(register_1_q[2]), .In_2(register_1_q[1]), .In_3(register_1_q[0]), .In(in_1), .O1(out_2),
    .O2(out_3), .O3(out_4));
endmodule

module S0 (
  input  In_1,
  input  In_2,
  input  In_3,
  input  In,
  output O1,
  output O2,
  output O3
);

  wire and_1_out, and_2_out, and_3_out, and_4_out, and_5_out, and_6_out, and_7_out, and_8_out, and_9_out,
       not_1_out, not_2_out, not_3_out, not_4_out;

  and and_1 (and_1_out, In_2, not_1_out);
  not not_1 (not_1_out, In);
  and and_2 (and_2_out, In_1, In_3);
  and and_3 (and_3_out, In_1, In_2);
  and and_4 (and_4_out, In_1, In_3);
  and and_5 (and_5_out, In_1, In_2);
  not not_2 (not_2_out, In_2);
  and and_6 (and_6_out, not_2_out, not_3_out);
  not not_3 (not_3_out, In);
  and and_7 (and_7_out, In_2, In);
  and and_8 (and_8_out, In_1, not_4_out);
  not not_4 (not_4_out, In);
  and and_9 (and_9_out, In_1, In_3);
  or or_1 (O1, and_1_out, and_2_out, and_3_out);
  or or_2 (O2, In, and_4_out, and_5_out);
  or or_3 (O3, and_6_out, and_7_out, and_8_out, and_9_out);
endmodule

module mod5 (
  input  In,
  output S0,
  output S1,
  output S2,
  output S3,
  output S4
);

  wire s1_1_out_2, s1_1_out_3, s1_1_out_4;

  S2 s2_1 (.I0(s1_1_out_2), .I1(s1_1_out_3), .I2(s1_1_out_4), .O1(S0), .O2(S1), .O3(S2), .O4(S3), .O5(S4));
  S1 s1_1 (.in_1(In), .out_2(s1_1_out_2), .out_3(s1_1_out_3), .out_4(s1_1_out_4));
endmodule

module S2 (
  input  I0,
  input  I1,
  input  I2,
  output O1,
  output O2,
  output O3,
  output O4,
  output O5
);

  wire and_2_out, and_3_out, not_1_out, not_2_out, not_3_out, not_4_out;

  not not_1 (not_1_out, I0);
  not not_2 (not_2_out, I1);
  not not_3 (not_3_out, I1);
  not not_4 (not_4_out, I2);
  and and_1 (O4, I1, I2);
  and and_2 (and_2_out, not_1_out, not_2_out);
  and and_3 (and_3_out, not_3_out, I2);
  and and_4 (O3, I1, not_4_out);
  or or_1 (O2, and_2_out, and_3_out);

  assign O1 = 1'b0;
  assign O5 = I0;
endmodule

module Test (
  output out_1,
  output out_2,
  output out_3,
  output out_4,
  output out_5,
  output out_6,
  output out_7
);

  wire clock_1_out;
  wire [3:0] counter_1_q;

  Counter #(.width(4), .max('hf)) counter_1 (
    .Q(counter_1_q), .carry(out_7), .clk(clock_1_out));  // open: load, D, count, clr
  Clock clock_1 (.out(clock_1_out));
  ROM #(.addrWidth(4), .dataWidth(1)) rom_1 (.addr(counter_1_q), .data(out_1));  // open: sel
  mod5 mod5_1 (.In(out_1), .S0(out_2), .S1(out_3), .S2(out_4), .S3(out_5), .S4(out_6));

  // Notes on the sheet:
  //   contents of rom_1 (hex, n*v repeats v):
  //   0 1 0 0 1 0 0 1 0 0 1 0 0 1
endmodule
