// Logisim project 2mod52.circ as structural Verilog: 3 circuits, main circuit mod5
module mod5 (
  input  in_1,
  output out_2,
  output out_3,
  output out_4,
  output out_5,
  output out_6
);

  wire clock_1_out, register_1_q;
  wire [1:0] s0_1_o2;

  Clock clock_1 (.out(clock_1_out));
  Register #(.width(1)) register_1 (.D(in_1), .Q(register_1_q), .clk(clock_1_out));  // open: en, clr
  Decoder #(.select(2)) decoder_1 (.out0(out_3), .out1(out_4), .out2(out_5), .out3(out_6), .sel(s0_1_o2));  // open: en
  // Probe on s0_1_o2
  S0 s0_1 (.S2(register_1_q), .S3(in_1), .O1(s0_1_o2[1]), .O2(s0_1_o2[0]));

  assign out_2 = 1'b0;
endmodule

module S0 (
  input  S2,
  input  S3,
  output O1,
  output O2
);

  wire and_1_out, and_2_out, not_1_out, not_2_out;

  not not_1 (not_1_out, S2);
  not not_2 (not_2_out, S3);
  and and_1 (and_1_out, not_1_out, S3);
  and and_2 (and_2_out, S2, not_2_out);
  or or_1 (O2, and_1_out, and_2_out);

  assign O1 = S2;
endmodule

module Test (
  output out_1,
  output out_2,
  output out_3,
  output out_4,
  output out_5,
  output out_6
);

  wire clock_1_out, rom_1_data;
  wire [3:0] counter_1_q;

  Clock clock_1 (.out(clock_1_out));
  Counter #(.width(4), .max('hf)) counter_1 (
    .Q(counter_1_q), .carry(out_6), .clk(clock_1_out));  // open: load, D, count, clr
  ROM #(.addrWidth(4), .dataWidth(1)) rom_1 (.addr(counter_1_q), .data(rom_1_data));  // open: sel
  mod5 mod5_1 (.in_1(rom_1_data), .out_2(out_1), .out_3(out_2), .out_4(out_3), .out_5(out_4), .out_6(out_5));

  // Notes on the sheet:
  //   contents of rom_1 (hex, n*v repeats v):
  //   0 1 0 0 1 0 0 1 0 0 1 0 0 1
endmodule
