// Logisim project CHALLENGE.circ as structural Verilog: 4 circuits, main circuit main
module main (
  input  [31:0] in_1,
  output [31:0] out_2
);

  wire clock_1_out, comparator_1_eq, comparator_2_eq, not_1_out;
  wire [31:0] counter_1_q, jzjs_1_out_5, jzjs_2_out_5, jzjs_3_out_5, jzjs_4_out_5, multiplexer_1_out,
       s0_1_out_2, s0_2_out_2, s0_3_out_2, s1_1_out_2;

  // Probe on in_1
  not not_1 (not_1_out, clock_1_out);
  Clock clock_1 (.out(clock_1_out));
  JZJS jzjs_1 (.in_1(s0_1_out_2), .in_2({32{1'b0}}), .in_3(s0_2_out_2), .in_4(32'h1), .out_5(jzjs_1_out_5));
  JZJS jzjs_2 (.in_1(s0_1_out_2), .in_2(32'h1), .in_3(s0_2_out_2), .in_4(32'h1), .out_5(jzjs_2_out_5));
  JZJS jzjs_3 (.in_1(s1_1_out_2), .in_2({32{1'b0}}), .in_3(s0_3_out_2), .in_4(32'h1), .out_5(jzjs_3_out_5));
  JZJS jzjs_4 (.in_1(s1_1_out_2), .in_2(32'h1), .in_3(s0_3_out_2), .in_4(32'h1), .out_5(jzjs_4_out_5));
  Counter #(.width(32), .max('hffffffff)) counter_1 (
    .Q(counter_1_q), .clk(not_1_out));  // open: load, D, count, carry, clr
  Comparator #(.width(32), .mode("unsigned")) comparator_1 (
    .a(in_1), .b(counter_1_q), .eq(comparator_1_eq));  // open: gt, lt
  S0 s0_1 (.in_1(jzjs_1_out_5), .out_2(s0_1_out_2));
  S0 s0_2 (.in_1(jzjs_2_out_5), .out_2(s0_2_out_2));
  S1 s1_1 (.in_1(jzjs_3_out_5), .out_2(s1_1_out_2));
  S0 s0_3 (.in_1(jzjs_4_out_5), .out_2(s0_3_out_2));
  Comparator #(.width(32), .mode("unsigned")) comparator_2 (
    .a(in_1), .b({32{1'b0}}), .eq(comparator_2_eq));  // open: gt, lt
  Multiplexer #(.width(32)) multiplexer_1 (
    .in0({32{1'b0}}), .in1(s1_1_out_2), .out(multiplexer_1_out), .sel(comparator_1_eq));  // open: en
  Multiplexer #(.width(32)) multiplexer_2 (
    .in0(multiplexer_1_out), .in1({32{1'b0}}), .out(out_2), .sel(comparator_2_eq));  // open: en
endmodule

module JZJS (
  input  [31:0] in_1,
  input  [31:0] in_2,
  input  [31:0] in_3,
  input  [31:0] in_4,
  output [31:0] out_5
);

  wire [31:0] multiplier_1_out, multiplier_2_out;

  Multiplier #(.width(32)) multiplier_1 (.a(in_1), .b(in_2), .out(multiplier_1_out));  // open: cin, cout
  Multiplier #(.width(32)) multiplier_2 (.a(in_3), .b(in_4), .out(multiplier_2_out));  // open: cin, cout
  Adder #(.width(32)) adder_1 (.a(multiplier_1_out), .b(multiplier_2_out), .out(out_5));  // open: cin, cout
endmodule

module S0 (
  input  [31:0] in_1,
  output [31:0] out_2
);

  wire clock_1_out, comparator_1_eq, not_1_out, not_2_out;
  wire [31:0] demultiplexer_1_out0, demultiplexer_1_out1, multiplexer_1_out, register_1_q, register_2_q;

  Demultiplexer #(.width(32)) demultiplexer_1 (
    .out0(demultiplexer_1_out0), .out1(demultiplexer_1_out1), .in(in_1), .sel(clock_1_out));  // open: en
  Register #(.width(32)) register_1 (.D(demultiplexer_1_out0), .Q(register_1_q), .clk(clock_1_out));  // open: en, clr
  Register #(.width(32)) register_2 (.D(demultiplexer_1_out1), .Q(register_2_q), .clk(not_1_out));  // open: en, clr
  not not_1 (not_1_out, clock_1_out);
  Clock clock_1 (.out(clock_1_out));
  Multiplexer #(.width(32)) multiplexer_1 (
    .in0(register_1_q), .in1(register_2_q), .out(multiplexer_1_out), .sel(clock_1_out));  // open: en
  Comparator #(.width(32), .mode("unsigned")) comparator_1 (
    .a({32{1'b0}}), .b(multiplexer_1_out), .eq(comparator_1_eq));  // open: gt, lt
  Multiplexer #(.width(32)) multiplexer_2 (
    .in0(32'h1), .in1(multiplexer_1_out), .out(out_2), .sel(not_2_out));  // open: en
  not not_2 (not_2_out, comparator_1_eq);
endmodule

module S1 (
  input  [31:0] in_1,
  output [31:0] out_2
);

  wire clock_1_out, not_1_out;
  wire [31:0] demultiplexer_1_out0, demultiplexer_1_out1, register_1_q, register_2_q;

  Demultiplexer #(.width(32)) demultiplexer_1 (
    .out0(demultiplexer_1_out0), .out1(demultiplexer_1_out1), .in(in_1), .sel(clock_1_out));  // open: en
  Register #(.width(32)) register_1 (.D(demultiplexer_1_out0), .Q(register_1_q), .clk(clock_1_out));  // open: en, clr
  Register #(.width(32)) register_2 (.D(demultiplexer_1_out1), .Q(register_2_q), .clk(not_1_out));  // open: en, clr
  not not_1 (not_1_out, clock_1_out);
  Clock clock_1 (.out(clock_1_out));
  Multiplexer #(.width(32)) multiplexer_1 (
    .in0(register_1_q), .in1(register_2_q), .out(out_2), .sel(clock_1_out));  // open: en
endmodule
