// Logisim project cou.circ as structural Verilog: 8 circuits, main circuit main
module main (
  input  Reset,
  output [31:0] Instr,
  output RegWrite,
  output [4:0] RegAddr,
  output [31:0] RegData,
  output MemWrite,
  output [4:0] MemAdress,
  output [31:0] MenData
);

  wire addu, ALUsrc, beq, Branch, Clk, ExtOp, j, jal, Jump, lui, lw, MemtoReg, ori, PCSrc, RegDst, subu, sw,
       swl, Zero;
  wire [1:0] ALUOp;
  wire [4:0] bit_extender_1_out, multiplexer_2_out, PC;
  wire [31:0] adder_1_out, ALUResult, ext_1_out_3, JPC, multiplexer_5_out, NPC, PC4, RD1, RegIn,
       shifter_1_out, WD3;

  Clock clock_1 (.out(Clk));
  // Probe on ori
  // Probe on PC
  // Probe on addu
  // Probe on subu
  PC pc_1 (.NPC(NPC), .JPC(JPC), .PCSrc(PCSrc), .Jump(Jump), .Clk(Clk), .Reset(Reset), .out_7(PC4), .out_8(PC));
  // Probe on sw
  // Probe on lw
  ROM #(.addrWidth(5), .dataWidth(32)) rom_1 (.addr(PC), .data(Instr));  // open: sel
  Subtractor #(.width(32)) subtractor_1 (
    .a({PC4[31:28], Instr[25:0], 2'b00}), .b(32'h3000), .out(JPC));  // open: bin, bout
  // Probe on j
  // Probe on beq
  // Probe on MenData
  // Probe on bit_extender_1_out
  Bit_Extender #(.in_width(32), .out_width(5)) bit_extender_1 (
    .in({ALUResult[31:7], MemAdress, ALUResult[1:0]}), .out(bit_extender_1_out));
  and and_1 (PCSrc, Branch, Zero);
  ORAND orand_1 (
    .in_1(Instr[31:26]), .ori(ori), .addu(addu), .subu(subu), .lw(lw), .sw(sw), .beq(beq), .lui(lui),
    .MemtoReg(MemtoReg), .RegDst(RegDst), .ALUSrc(ALUsrc), .Regwrite(RegWrite), .Memwrite(MemWrite),
    .Branch(Branch), .ExtOp(ExtOp), .ALUOp(ALUOp), .Jump(Jump), .j(j), .jal(jal), .swl(swl));
  // Probe on RegIn
  RAM #(.addrWidth(5), .dataWidth(32), .bus("separate")) ram_1 (
    .addr(bit_extender_1_out), .din(MenData), .data(RegIn), .str(MemWrite), .clk(Clk), .ld(RegWrite),
    .clr(Reset));  // open: sel
  Multiplexer #(.width(32), .disabled(0), .enable("false")) multiplexer_1 (
    .in0({ALUResult[31:7], MemAdress, ALUResult[1:0]}), .in1(RegIn), .out(WD3), .sel(MemtoReg));
  Multiplexer #(.width(5), .disabled(0), .enable("false")) multiplexer_2 (
    .in0(Instr[20:16]), .in1(Instr[15:11]), .out(multiplexer_2_out), .sel(RegDst));
  Multiplexer #(.width(5), .disabled(0), .enable("false")) multiplexer_3 (
    .in0(multiplexer_2_out), .in1({5{1'b1}}), .out(RegAddr), .sel(jal));
  Adder #(.width(32)) adder_1 (.a(PC4), .b(32'h3004), .out(adder_1_out));  // open: cin, cout
  Multiplexer #(.width(32), .disabled(0), .enable("false")) multiplexer_4 (
    .in0(WD3), .in1(adder_1_out), .out(RegData), .sel(jal));
  // Probe on ext_1_out_3
  EXT ext_1 (.in_2(Instr[15:0]), .ExtOp(ExtOp), .out_3(ext_1_out_3));
  GRF grf_1 (
    .A1(Instr[25:21]), .A2(Instr[20:16]), .A3(RegAddr), .WD3(RegData), .Clk(Clk), .WE3(RegWrite),
    .Reset(Reset), .RD1(RD1), .RD2(MenData));  // open: RegData
  // Probe on MenData
  Multiplexer #(.width(32), .disabled(0), .enable("false")) multiplexer_5 (
    .in0(MenData), .in1(ext_1_out_3), .out(multiplexer_5_out), .sel(ALUsrc));
  Shifter #(.width(32)) shifter_1 (.in(ext_1_out_3), .\dist (5'b00010), .out(shifter_1_out));
  ALU alu_1 (
    .in_4(RD1), .in_5(multiplexer_5_out), .ALUResult({ALUResult[31:7], MemAdress, ALUResult[1:0]}),
    .ALUOp(ALUOp), .func(Instr[5:0]), .Opencode(Instr[31:26]), .Zero(Zero));
  // Probe on {ALUResult[31:7], MemAdress, ALUResult[1:0]}
  Adder #(.width(32)) adder_2 (.a(shifter_1_out), .b(PC4), .out(NPC));  // open: cin, cout
  // Probe on NPC

  // Other names for the same wires on the sheet: _0_5[5:0] = Instr[5:0]; address[25:0] = Instr[25:0];
  //   func[5:0] = Instr[5:0]; immediate[15:0] = Instr[15:0]; _6_10[4:0] = Instr[10:6]; shamt[4:0] = Instr[10:6];
  //   _11_15[4:0] = Instr[15:11]; rd[4:0] = Instr[15:11]; _16_20[4:0] = Instr[20:16]; rt[4:0] = Instr[20:16];
  //   _21_25[4:0] = Instr[25:21]; rs[4:0] = Instr[25:21]; ALUResult[6:2] = MemAdress; _26_31[5:0] = Instr[31:26];
  //   op[5:0] = Instr[31:26]; RD2[31:0] = MenData

  // Notes on the sheet:
  //   contents of rom_1 (hex, n*v repeats v):
  //   3c090001 3c0a0002 12a5821 1495823 352d0064 adcd0000 8dcf0000 c000c04
endmodule

module PC (
  input  PCSrc,
  input  Jump,
  input  Clk,
  input  Reset,
  input  [31:0] NPC,
  input  [31:0] JPC,
  output [31:0] out_7,
  output [4:0] out_8
);

  wire [31:0] adder_1_out, multiplexer_1_out, multiplexer_2_out, shifter_1_out;

  Multiplexer #(.width(32), .disabled(0), .enable("false")) multiplexer_1 (
    .in0(out_7), .in1(NPC), .out(multiplexer_1_out), .sel(PCSrc));
  Multiplexer #(.width(32), .disabled(0), .enable("false")) multiplexer_2 (
    .in0(multiplexer_1_out), .in1(JPC), .out(multiplexer_2_out), .sel(Jump));
  Adder #(.width(32)) adder_1 (.a(multiplexer_2_out), .b(32'h4), .out(adder_1_out));  // open: cin, cout
  Register #(.width(32)) register_1 (.D(adder_1_out), .Q(out_7), .clk(Clk), .clr(Reset));  // open: en
  Shifter #(.width(32), .shift("lr")) shifter_1 (.in(out_7), .\dist (5'b00010), .out(shifter_1_out));
  Bit_Extender #(.in_width(32), .out_width(5)) bit_extender_1 (.in(shifter_1_out), .out(out_8));

  // Other names for the same wires on the sheet: PC[4:0] = out_8; PC4[31:0] = out_7
endmodule

module ORAND (
  input  [5:0] in_1,
  output MemtoReg,
  output ori,
  output addu,
  output subu,
  output lw,
  output sw,
  output beq,
  output lui,
  output j,
  output jal,
  output swl,
  output [1:0] ALUOp,
  output RegDst,
  output ALUSrc,
  output Regwrite,
  output Memwrite,
  output Branch,
  output ExtOp,
  output Jump
);

  wire not_1_out, not_2_out, not_3_out, not_4_out, not_5_out, not_6_out;

  not not_1 (not_1_out, in_1[5]);
  not not_2 (not_2_out, in_1[3]);
  not not_3 (not_3_out, in_1[4]);
  not not_4 (not_4_out, in_1[2]);
  not not_5 (not_5_out, in_1[0]);
  not not_6 (not_6_out, in_1[1]);
  and u_ori (ori, not_1_out, not_3_out, in_1[3], in_1[2], not_6_out, in_1[0]);
  and u_addu (addu, not_1_out, not_3_out, not_2_out, not_4_out, not_6_out, not_5_out);
  and u_subu (subu, not_1_out, not_3_out, not_2_out, not_4_out, not_6_out, not_5_out);
  and u_lw (lw, in_1[5], not_3_out, not_2_out, not_4_out, in_1[1], in_1[0]);
  and u_sw (sw, in_1[5], not_3_out, in_1[3], not_4_out, in_1[1], in_1[0]);
  and u_beq (ALUOp[0], not_1_out, not_3_out, not_2_out, in_1[2], not_6_out, not_5_out);
  and u_lui (lui, not_1_out, not_3_out, in_1[3], in_1[2], in_1[1], in_1[0]);
  and u_j (j, not_1_out, not_3_out, not_2_out, not_4_out, in_1[1], not_5_out);
  and u_jal (jal, not_1_out, not_3_out, not_2_out, not_4_out, in_1[1], in_1[0]);
  and u_swl (swl, in_1[5], not_3_out, in_1[3], not_4_out, in_1[1], in_1[0]);
  or u_RegDst (RegDst, addu, subu);
  or u_ALUSrc (ALUSrc, sw, lw, ori, lui);
  or u_Regwrite (Regwrite, addu, subu, lui, ori, lw, jal);
  or u_Memwrite (Memwrite, sw, swl);
  or u_ExtOp (ExtOp, lw, sw, sw);
  or if_1 (ALUOp[1], addu, subu);
  or u_Jump (Jump, j, jal);

  assign beq = ALUOp[0];
  assign Branch = ALUOp[0];
  assign MemtoReg = lw;

  // Other names for the same wires on the sheet: if_2 = ALUOp[0]; if_1 = ALUOp[1]; op0 = in_1[0]; op1 = in_1[1];
  //   op2 = in_1[2]; op3 = in_1[3]; op4 = in_1[4]; op5 = in_1[5]
endmodule

module GRF (
  input  Clk,
  input  WE3,
  input  Reset,
  input  [4:0] A1,
  input  [4:0] A2,
  input  [4:0] A3,
  input  [31:0] WD3,
  output [31:0] RD1,
  output [31:0] RD2,
  output [31:0] RegData
);

  wire Regwrite1, Regwrite2, Regwrite3, Regwrite4, Regwrite5, Regwrite6, Regwrite7, Regwrite8, Regwrite9,
       Regwrite10, Regwrite11, Regwrite12, Regwrite13, Regwrite14, Regwrite15, Regwrite16, Regwrite17,
       Regwrite18, Regwrite19, Regwrite20, Regwrite21, Regwrite22, Regwrite23, Regwrite24, Regwrite25,
       Regwrite26, Regwrite27, Regwrite28, Regwrite29, Regwrite30, Regwrite31;
  wire [31:0] RegOut0, RegOut1, RegOut2, RegOut3, RegOut4, RegOut5, RegOut6, RegOut7, RegOut8, RegOut9,
       RegOut10, RegOut11, RegOut12, RegOut13, RegOut14, RegOut15, RegOut16, RegOut17, RegOut18, RegOut19,
       RegOut20, RegOut21, RegOut22, RegOut23, RegOut24, RegOut25, RegOut26, RegOut27, RegOut28, RegOut29,
       RegOut30, RegOut31;

  Multiplexer #(.select(5), .width(32), .enable("false")) multiplexer_1 (
    .in0(RegOut0), .in1(RegOut1), .in2(RegOut2), .in3(RegOut3), .in4(RegOut4), .in5(RegOut5), .in6(RegOut6),
    .in7(RegOut7), .in8(RegOut8), .in9(RegOut9), .in10(RegOut10), .in11(RegOut11), .in12(RegOut12),
    .in13(RegOut13), .in14(RegOut14), .in15(RegOut15), .in16(RegOut16), .in17(RegOut17), .in18(RegOut18),
    .in19(RegOut19), .in20(RegOut20), .in21(RegOut21), .in22(RegOut22), .in23(RegOut23), .in24(RegOut24),
    .in25(RegOut25), .in26(RegOut26), .in27(RegOut27), .in28(RegOut28), .in29(RegOut29), .in30(RegOut30),
    .in31(RegOut31), .out(RD1), .sel(A1));
  Multiplexer #(.select(5), .width(32), .enable("false")) multiplexer_2 (
    .in0(RegOut0), .in1(RegOut1), .in2(RegOut2), .in3(RegOut3), .in4(RegOut4), .in5(RegOut5), .in6(RegOut6),
    .in7(RegOut7), .in8(RegOut8), .in9(RegOut9), .in10(RegOut10), .in11(RegOut11), .in12(RegOut12),
    .in13(RegOut13), .in14(RegOut14), .in15(RegOut15), .in16(RegOut16), .in17(RegOut17), .in18(RegOut18),
    .in19(RegOut19), .in20(RegOut20), .in21(RegOut21), .in22(RegOut22), .in23(RegOut23), .in24(RegOut24),
    .in25(RegOut25), .in26(RegOut26), .in27(RegOut27), .in28(RegOut28), .in29(RegOut29), .in30(RegOut30),
    .in31(RegOut31), .out(RegData), .sel(A3));
  Multiplexer #(.select(5), .width(32), .enable("false")) multiplexer_3 (
    .in0(RegOut0), .in1(RegOut1), .in2(RegOut2), .in3(RegOut3), .in4(RegOut4), .in5(RegOut5), .in6(RegOut6),
    .in7(RegOut7), .in8(RegOut8), .in9(RegOut9), .in10(RegOut10), .in11(RegOut11), .in12(RegOut12),
    .in13(RegOut13), .in14(RegOut14), .in15(RegOut15), .in16(RegOut16), .in17(RegOut17), .in18(RegOut18),
    .in19(RegOut19), .in20(RegOut20), .in21(RegOut21), .in22(RegOut22), .in23(RegOut23), .in24(RegOut24),
    .in25(RegOut25), .in26(RegOut26), .in27(RegOut27), .in28(RegOut28), .in29(RegOut29), .in30(RegOut30),
    .in31(RegOut31), .out(RD2), .sel(A2));
  Decoder #(.select(5), .disabled(0)) decoder_1 (
    .out1(Regwrite1), .out2(Regwrite2), .out3(Regwrite3), .out4(Regwrite4), .out5(Regwrite5),
    .out6(Regwrite6), .out7(Regwrite7), .out8(Regwrite8), .out9(Regwrite9), .out10(Regwrite10),
    .out11(Regwrite11), .out12(Regwrite12), .out13(Regwrite13), .out14(Regwrite14), .out15(Regwrite15),
    .out16(Regwrite16), .out17(Regwrite17), .out18(Regwrite18), .out19(Regwrite19), .out20(Regwrite20),
    .out21(Regwrite21), .out22(Regwrite22), .out23(Regwrite23), .out24(Regwrite24), .out25(Regwrite25),
    .out26(Regwrite26), .out27(Regwrite27), .out28(Regwrite28), .out29(Regwrite29), .out30(Regwrite30),
    .out31(Regwrite31), .sel(A3), .en(WE3));  // open: out0
  Register #(.width(32)) register_1 (.D({32{1'b0}}), .Q(RegOut0), .clk(Clk), .clr(Reset));  // open: en
  Register #(.width(32)) register_2 (.D(WD3), .en(Regwrite4), .Q(RegOut4), .clk(Clk), .clr(Reset));
  Register #(.width(32)) register_3 (.D(WD3), .en(Regwrite8), .Q(RegOut8), .clk(Clk), .clr(Reset));
  Register #(.width(32)) register_4 (.D(WD3), .en(Regwrite12), .Q(RegOut12), .clk(Clk), .clr(Reset));
  Register #(.width(32)) register_5 (.D(WD3), .en(Regwrite16), .Q(RegOut16), .clk(Clk), .clr(Reset));
  Register #(.width(32)) register_6 (.D(WD3), .en(Regwrite20), .Q(RegOut20), .clk(Clk), .clr(Reset));
  Register #(.width(32)) register_7 (.D(WD3), .en(Regwrite24), .Q(RegOut24), .clk(Clk), .clr(Reset));
  Register #(.width(32)) register_8 (.D(WD3), .en(Regwrite28), .Q(RegOut28), .clk(Clk), .clr(Reset));
  Register #(.width(32)) register_9 (.D(WD3), .en(Regwrite1), .Q(RegOut1), .clk(Clk), .clr(Reset));
  Register #(.width(32)) register_10 (.D(WD3), .en(Regwrite5), .Q(RegOut5), .clk(Clk), .clr(Reset));
  Register #(.width(32)) register_11 (.D(WD3), .en(Regwrite9), .Q(RegOut9), .clk(Clk), .clr(Reset));
  Register #(.width(32)) register_12 (.D(WD3), .en(Regwrite13), .Q(RegOut13), .clk(Clk), .clr(Reset));
  Register #(.width(32)) register_13 (.D(WD3), .en(Regwrite17), .Q(RegOut17), .clk(Clk), .clr(Reset));
  Register #(.width(32)) register_14 (.D(WD3), .en(Regwrite21), .Q(RegOut21), .clk(Clk), .clr(Reset));
  Register #(.width(32)) register_15 (.D(WD3), .en(Regwrite25), .Q(RegOut25), .clk(Clk), .clr(Reset));
  Register #(.width(32)) register_16 (.D(WD3), .en(Regwrite29), .Q(RegOut29), .clk(Clk), .clr(Reset));
  Register #(.width(32)) register_17 (.D(WD3), .en(Regwrite2), .Q(RegOut2), .clk(Clk), .clr(Reset));
  Register #(.width(32)) register_18 (.D(WD3), .en(Regwrite6), .Q(RegOut6), .clk(Clk), .clr(Reset));
  Register #(.width(32)) register_19 (.D(WD3), .en(Regwrite10), .Q(RegOut10), .clk(Clk), .clr(Reset));
  Register #(.width(32)) register_20 (.D(WD3), .en(Regwrite14), .Q(RegOut14), .clk(Clk), .clr(Reset));
  Register #(.width(32)) register_21 (.D(WD3), .en(Regwrite18), .Q(RegOut18), .clk(Clk), .clr(Reset));
  Register #(.width(32)) register_22 (.D(WD3), .en(Regwrite22), .Q(RegOut22), .clk(Clk), .clr(Reset));
  Register #(.width(32)) register_23 (.D(WD3), .en(Regwrite26), .Q(RegOut26), .clk(Clk), .clr(Reset));
  Register #(.width(32)) register_24 (.D(WD3), .en(Regwrite30), .Q(RegOut30), .clk(Clk), .clr(Reset));
  Register #(.width(32)) register_25 (.D(WD3), .en(Regwrite3), .Q(RegOut3), .clk(Clk), .clr(Reset));
  Register #(.width(32)) register_26 (.D(WD3), .en(Regwrite7), .Q(RegOut7), .clk(Clk), .clr(Reset));
  Register #(.width(32)) register_27 (.D(WD3), .en(Regwrite11), .Q(RegOut11), .clk(Clk), .clr(Reset));
  Register #(.width(32)) register_28 (.D(WD3), .en(Regwrite15), .Q(RegOut15), .clk(Clk), .clr(Reset));
  Register #(.width(32)) register_29 (.D(WD3), .en(Regwrite19), .Q(RegOut19), .clk(Clk), .clr(Reset));
  Register #(.width(32)) register_30 (.D(WD3), .en(Regwrite23), .Q(RegOut23), .clk(Clk), .clr(Reset));
  Register #(.width(32)) register_31 (.D(WD3), .en(Regwrite27), .Q(RegOut27), .clk(Clk), .clr(Reset));
  Register #(.width(32)) register_32 (.D(WD3), .en(Regwrite31), .Q(RegOut31), .clk(Clk), .clr(Reset));
  // Probe on RegOut31

  // Other names for the same wires on the sheet: Clr = Reset; RegIn[31:0] = WD3; Regwrite = WE3
endmodule

module ALU (
  input  [1:0] ALUOp,
  input  [5:0] func,
  input  [5:0] Opencode,
  input  [31:0] in_4,
  input  [31:0] in_5,
  output Zero,
  output [31:0] ALUResult
);

  wire [2:0] model2_1_o3;
  wire [31:0] _1, _2, _3, _4, ADDU, AND, ORI, Result1, SUBU, temp;

  model2 model2_1 (
    .F3(func[3]), .F4(func[2]), .F5(func[1]), .F6(func[0]), .O1(model2_1_o3[2]), .O2(model2_1_o3[1]),
    .O3(model2_1_o3[0]));
  Multiplexer #(.select(2), .width(32), .disabled(0), .enable("false")) multiplexer_1 (
    .in0(_1), .in1(_2), .in2(_3), .in3(_4), .out(Result1), .sel(Opencode[5:4]));
  Multiplexer #(.select(4), .width(32), .disabled(0), .enable("false")) multiplexer_2 (
    .in4(SUBU), .in13(ORI), .in15({in_5[15:0], {16{1'b0}}}), .out(_1), .sel(Opencode[3:0]));  // open: in0, in1, in2, in3, in5, in6, in7, in8, in9, in10, in11, in12, in14
  Multiplexer #(.select(3), .width(32), .disabled(0), .enable("false")) multiplexer_3 (
    .in0(AND), .in2(ADDU), .in6(SUBU), .out(temp), .sel(model2_1_o3));  // open: in1, in3, in4, in5, in7
  Multiplexer #(.select(4), .width(32), .disabled(0), .enable("false")) multiplexer_4 (
    .out(_2), .sel(Opencode[3:0]));  // open: in0, in1, in2, in3, in4, in5, in6, in7, in8, in9, in10, in11, in12, in13, in14, in15
  Multiplexer #(.select(2), .width(32), .enable("false")) multiplexer_5 (
    .in0(Result1), .in1(SUBU), .in2(temp), .out(ALUResult), .sel(ALUOp));  // open: in3
  // Probe on ALUOp
  Adder #(.width(32)) adder_1 (.a(in_4), .b(in_5), .out(ADDU));  // open: cin, cout
  Subtractor #(.width(32)) subtractor_1 (.a(in_4), .b(in_5), .out(SUBU));  // open: bin, bout
  assign ORI = in_4 | in_5;  // OR_Gate or_1, 32 bits wide
  assign AND = in_4 & in_5;  // AND_Gate and_1, 32 bits wide
  Comparator #(.width(32), .mode("unsigned")) comparator_1 (.a(in_4), .b(in_5), .eq(Zero));  // open: gt, lt
  Multiplexer #(.select(4), .width(32), .disabled(0), .enable("false")) multiplexer_6 (
    .in3(ADDU), .in11(ADDU), .out(_3), .sel(Opencode[3:0]));  // open: in0, in1, in2, in4, in5, in6, in7, in8, in9, in10, in12, in13, in14, in15
  // Probe on in_5[15:0]
  Multiplexer #(.select(4), .width(32), .disabled(0), .enable("false")) multiplexer_7 (
    .out(_4), .sel(Opencode[3:0]));  // open: in0, in1, in2, in3, in4, in5, in6, in7, in8, in9, in10, in11, in12, in13, in14, in15

  // Other names for the same wires on the sheet: IN1[31:0] = in_4; IN2[31:0] = in_5; LUI[31:16] = in_5[15:0];
  //   _0_3[3:0] = Opencode[3:0]; _4_5[1:0] = Opencode[5:4]
endmodule

module EXT (
  input  ExtOp,
  input  [15:0] in_2,
  output [31:0] out_3
);

  wire [31:0] bit_extender_1_out, bit_extender_2_out;

  assign bit_extender_1_out = {{16{1'b0}}, in_2};  // Bit_Extender bit_extender_1
  assign bit_extender_2_out = {{16{in_2[15]}}, in_2};  // Bit_Extender bit_extender_2
  Multiplexer #(.width(32), .disabled(0), .enable("false")) multiplexer_1 (
    .in0(bit_extender_1_out), .in1(bit_extender_2_out), .out(out_3), .sel(ExtOp));
endmodule

module model1 (
  input  I1,
  input  I2,
  input  I3,
  output OP1,
  output OP2
);

  wire and_1_out, and_2_out, and_3_out, and_4_out, not_1_out, not_2_out, not_3_out, not_4_out, or_1_out,
       or_2_out;

  not not_1 (not_1_out, I1);
  not not_2 (not_2_out, I2);
  not not_3 (not_3_out, I1);
  not not_4 (not_4_out, I3);
  and and_1 (and_1_out, not_1_out, not_2_out);
  and and_2 (and_2_out, not_3_out, not_4_out);
  or or_1 (or_1_out, and_1_out, I3);
  and and_3 (and_3_out, I1, I2);
  or or_2 (or_2_out, and_2_out, I2);
  and and_4 (and_4_out, I1, I3);
  or or_3 (OP1, or_1_out, and_3_out);
  or or_4 (OP2, or_2_out, and_4_out);
endmodule

module model2 (
  input  F3,
  input  F4,
  input  F5,
  input  F6,
  output O1,
  output O2,
  output O3
);

  wire and_1_out, and_2_out, and_3_out, and_4_out, and_5_out, not_1_out, not_2_out, not_3_out, not_4_out,
       not_5_out;

  not not_1 (not_1_out, F4);
  and and_1 (and_1_out, F3, not_2_out, F6);
  not not_2 (not_2_out, F5);
  not not_3 (not_3_out, F3);
  and and_2 (and_2_out, not_3_out, F4, F6);
  and and_3 (and_3_out, F3, not_4_out);
  not not_4 (not_4_out, F4);
  and and_4 (and_4_out, F3, not_5_out);
  not not_5 (not_5_out, F6);
  and and_5 (and_5_out, F3, F5);
  or or_1 (O2, not_1_out, and_1_out);
  or or_2 (O3, and_2_out, and_3_out, and_4_out, and_5_out);

  assign O1 = F5;
endmodule
